// Logisim project ULA+Teclado.circ as structural Verilog: 1 circuit, main circuit main
module main (
  input  in_1,
  input  in_2,
  input  in_3,
  input  in_4,
  input  in_5,
  input  in_6,
  input  in_7,
  output out_8,
  output [6:0] out_9
);

  wire button_1_out, clock_1_out, clock_2_out, clock_3_out;
  wire [2:0] counter_1_q;
  wire [6:0] rom_1_data;

  Keyboard keyboard_1 (.clk(clock_1_out), .re(in_1), .clr(in_2), .avail(out_8), .data(out_9));
  Clock clock_1 (.out(clock_1_out));
  Clock clock_2 (.out(clock_2_out));
  TTY tty_1 (.data(out_9), .clk(clock_2_out), .we(in_3), .clr(in_4));
  Counter #(.width(3), .max('h3)) counter_1 (
    .load(in_5), .Q(counter_1_q), .clk(clock_3_out), .clr(button_1_out));  // open: D, count, carry
  Button button_1 (.out(button_1_out));
  Clock clock_3 (.out(clock_3_out));
  ROM #(.addrWidth(3), .dataWidth(7)) rom_1 (.addr(counter_1_q), .data(rom_1_data));  // open: sel
  TTY tty_2 (.data(rom_1_data), .clk(clock_3_out), .we(in_6), .clr(in_7));

  // Notes on the sheet:
  //   contents of rom_1 (hex, n*v repeats v):
  //   6f 69 a
endmodule
